// Digital circuit alu.dig as structural Verilog
// Arithmetic Logical unit.
// Performs all arithmetic operations.
// Used for arithmetic processor instructions as well as for 
// calculating memory addresses.
module alu (
  input  [31:0] SrcA,
  input  [31:0] SrcB,
  input  [2:0] ALUControl,
  output [31:0] Y,
  output Zero
);

  wire comparator_1_lt;
  wire [31:0] add_1_s, and_1_out, multiplexer_1_out, or_1_out, sub_1_s;

  Add #(.Bits(32)) add_1 (.a(SrcA), .b(SrcB), .c_i(1'b0), .s(add_1_s));  // open: c_o
  Sub #(.Bits(32)) sub_1 (.a(SrcA), .b(SrcB), .c_i(1'b0), .s(sub_1_s));  // open: c_o
  assign and_1_out = SrcA & SrcB;  // And and_1, 32 bits wide
  assign or_1_out = SrcA | SrcB;  // Or or_1, 32 bits wide
  Comparator #(.Signed("true"), .Bits(32)) comparator_1 (.a(SrcA), .b(SrcB), .lt(comparator_1_lt));  // open: gt, eq
  Multiplexer #(.Bits(32)) multiplexer_1 (
    .sel(comparator_1_lt), .in_0({32{1'b0}}), .in_1(32'h1), .out(multiplexer_1_out));
  Multiplexer #(.Selector_Bits(3), .Bits(32)) multiplexer_2 (
    .sel(ALUControl), .in_0(and_1_out), .in_1(or_1_out), .in_2(add_1_s), .in_3({32{1'b0}}),
    .in_4({32{1'b0}}), .in_5({32{1'b0}}), .in_6(sub_1_s), .in_7(multiplexer_1_out), .out(Y));
  Comparator #(.Signed("true"), .Bits(32)) comparator_2 (.a(Y), .b({32{1'b0}}), .eq(Zero));  // open: gt, lt

  // Other names for the same wires on the sheet: sel[2:0] = ALUControl

  // Notes on the sheet:
  //   SrcA: first operand
  //   SrcB: second operand
  //   ALUControl: selected operation
  //   Y: result of the operation
  //   Zero: Zero-flag. Is high if the relult is zero.
endmodule
