// Digital circuit dmem.dig as structural Verilog
module dmem (
  input  [31:0] A,
  input  [31:0] WD,
  input  WE,
  input  Clk,
  output [31:0] RD
);

  // RAM32Bit #(.generic("addrBits := 32;")) ram32bit_1: pin names not known; wires that end beside it: A, WD, WE, 1'b0, 1'b0, Clk, RD
endmodule
