// Digital circuit imem.dig as structural Verilog
module imem (
  input  [31:0] PC,
  input  Sel,
  output [31:0] Instr
);

  ROM #(.AddrBits(24), .isProgramMemory("true"), .Bits(32)) IMem (.A(PC[23:0]), .sel(Sel), .D(Instr));
  // Pins of 24 and 32 bits meet at PC
endmodule
