// Digital circuit mips.dig as structural Verilog
module mips (
);

  wire [31:0] imem_1_instr, pc_1_p1;

  // pc pc_1: pin names not known; wires that end beside it: pc_1_p1
  imem imem_1 (.PC(pc_1_p1), .Instr(imem_1_instr));  // open: Sel
  BitExtender bitextender_1 ();  // open: in, out
  // regfile regfile_1: pin names not known; wires that end beside it: imem_1_instr[20:16], imem_1_instr[25:21]
  alu alu_1 ();  // open: SrcA, SrcB, ALUControl, Y, Zero
  dmem dmem_1 ();  // open: A, WD, WE, Clk, RD
endmodule
