// Digital circuit pc.dig as structural Verilog
module pc (
  input  Clk,
  input  [31:0] ALU,
  input  rel,
  input  abs,
  output [31:0] Next,
  output [31:0] PC
);

  wire Reset_out;
  wire [31:0] add_1_s, multiplexer_1_out, multiplexer_2_out;

  Reset Reset (.out(Reset_out));
  Register #(.Bits(32), .isProgramCounter("true")) u_PC (.D(multiplexer_2_out), .C(~Clk), .en(Reset_out), .Q(PC));
  Add #(.Bits(32)) Increment (.a(PC), .b(32'h4), .c_i(1'b0), .s(Next));  // open: c_o
  Add #(.Bits(32)) add_1 (.a(Next), .b(ALU), .c_i(1'b0), .s(add_1_s));  // open: c_o
  Multiplexer #(.Bits(32)) multiplexer_1 (.sel(rel), .in_0(Next), .in_1(add_1_s), .out(multiplexer_1_out));
  Multiplexer #(.Bits(32)) multiplexer_2 (.sel(abs), .in_0(multiplexer_1_out), .in_1(ALU), .out(multiplexer_2_out));

  // Notes on the sheet:
  //   ALU: current ALU output
  //   rel: Triggers a relative jump.
  //   abs: Triggers an absolute jump.
endmodule
