// Digital circuit regfile.dig as structural Verilog
module regfile (
  input  Clk,
  input  [31:0] A2,
  input  [31:0] A1,
  input  [31:0] A3,
  input  WE,
  input  [31:0] WD3,
  output [31:0] RD1,
  output [31:0] RD2
);

  RegisterFile #(.AddrBits(24), .Bits(32)) RegFile (
    .Din(WD3), .we(WE), .Rw(A3[23:0]), .C(Clk), .Ra(A1[23:0]), .Rb(A2[23:0]), .Da(RD1), .Db(RD2));
  // Pins of 24 and 32 bits meet at A2
  // Pins of 24 and 32 bits meet at A1
  // Pins of 24 and 32 bits meet at A3
endmodule
