// Logisim project 4_bit_register_lr_shift.circ as structural Verilog: 1 circuit, main circuit register_4bits
module register_4bits (
  input  LR,
  input  SR,
  input  SL,
  input  [3:0] Data,
  input  Load,
  input  SE,
  input  clk,
  output [3:0] DataOut
);

  wire buffer_1_out, L0_out, L1_out, L2_out, L3_out, multiplexer_1_out, multiplexer_2_out, multiplexer_3_out,
       multiplexer_4_out, multiplexer_5_out, multiplexer_6_out, multiplexer_7_out, multiplexer_8_out,
       not_1_out, not_2_out, or_1_out, or_2_out, or_3_out, or_4_out, R0_out, R1_out, R2_out, R3_out;

  not not_1 (not_1_out, LR);
  not not_2 (not_2_out, not_1_out);
  and R3 (R3_out, SR, not_2_out);
  buf buffer_1 (buffer_1_out, clk);
  and L3 (L3_out, DataOut[2], not_1_out);
  or or_1 (or_1_out, R3_out, L3_out);
  Multiplexer multiplexer_1 (.in0(DataOut[3]), .in1(or_1_out), .out(multiplexer_1_out), .sel(SE));
  Multiplexer multiplexer_2 (.in0(multiplexer_1_out), .in1(Data[3]), .out(multiplexer_2_out), .sel(Load));
  D_Flip_Flop d_ff_1 (.D(multiplexer_2_out), .clk(buffer_1_out), .Q(DataOut[3]));  // open: Qn, preset, reset
  and R2 (R2_out, DataOut[3], not_2_out);
  or or_2 (or_2_out, R2_out, L2_out);
  and L2 (L2_out, DataOut[1], not_1_out);
  Multiplexer multiplexer_3 (.in0(DataOut[2]), .in1(or_2_out), .out(multiplexer_3_out), .sel(SE));
  D_Flip_Flop d_ff_2 (.D(multiplexer_4_out), .clk(buffer_1_out), .Q(DataOut[2]));  // open: Qn, preset, reset
  Multiplexer multiplexer_4 (.in0(multiplexer_3_out), .in1(Data[2]), .out(multiplexer_4_out), .sel(Load));
  and R1 (R1_out, DataOut[2], not_2_out);
  and L1 (L1_out, DataOut[0], not_1_out);
  or or_3 (or_3_out, R1_out, L1_out);
  Multiplexer multiplexer_5 (.in0(DataOut[1]), .in1(or_3_out), .out(multiplexer_5_out), .sel(SE));
  Multiplexer multiplexer_6 (.in0(multiplexer_5_out), .in1(Data[1]), .out(multiplexer_6_out), .sel(Load));
  D_Flip_Flop d_ff_3 (.D(multiplexer_6_out), .clk(buffer_1_out), .Q(DataOut[1]));  // open: Qn, preset, reset
  and R0 (R0_out, DataOut[1], not_2_out);
  or or_4 (or_4_out, R0_out, L0_out);
  and L0 (L0_out, SL, not_1_out);
  Multiplexer multiplexer_7 (.in0(DataOut[0]), .in1(or_4_out), .out(multiplexer_7_out), .sel(SE));
  Multiplexer multiplexer_8 (.in0(multiplexer_7_out), .in1(Data[0]), .out(multiplexer_8_out), .sel(Load));
  D_Flip_Flop d_ff_4 (.D(multiplexer_8_out), .clk(buffer_1_out), .Q(DataOut[0]));  // open: Qn, preset, reset
endmodule
