// Logisim project 8_bit_register.circ as structural Verilog: 1 circuit, main circuit register_8bits
module register_8bits (
  input  ENABLE,
  input  CLK,
  input  SHIFT_IN,
  input  SHIFT_ENABLE,
  input  [7:0] DATA,
  input  reset,
  output [7:0] DATA_OUT
);

  wire multiplexer_1_out, multiplexer_2_out, multiplexer_3_out, multiplexer_4_out, multiplexer_5_out,
       multiplexer_6_out, multiplexer_7_out, multiplexer_8_out, multiplexer_9_out, multiplexer_10_out,
       multiplexer_11_out, multiplexer_12_out, multiplexer_13_out, multiplexer_14_out, multiplexer_15_out,
       multiplexer_16_out;

  Multiplexer multiplexer_1 (.in0(DATA_OUT[7]), .in1(SHIFT_IN), .out(multiplexer_1_out), .sel(SHIFT_ENABLE));
  D_Flip_Flop d_ff_1 (.D(multiplexer_2_out), .clk(CLK), .Q(DATA_OUT[7]), .reset(reset));  // open: Qn, preset
  Multiplexer multiplexer_2 (.in0(multiplexer_1_out), .in1(DATA[7]), .out(multiplexer_2_out), .sel(ENABLE));
  Multiplexer multiplexer_3 (.in0(DATA_OUT[6]), .in1(DATA_OUT[7]), .out(multiplexer_3_out), .sel(SHIFT_ENABLE));
  D_Flip_Flop d_ff_2 (.D(multiplexer_4_out), .clk(CLK), .Q(DATA_OUT[6]), .reset(reset));  // open: Qn, preset
  Multiplexer multiplexer_4 (.in0(multiplexer_3_out), .in1(DATA[6]), .out(multiplexer_4_out));  // open: sel
  Multiplexer multiplexer_5 (.in0(DATA_OUT[5]), .in1(DATA_OUT[6]), .out(multiplexer_5_out), .sel(SHIFT_ENABLE));
  D_Flip_Flop d_ff_3 (.D(multiplexer_6_out), .clk(CLK), .Q(DATA_OUT[5]), .reset(reset));  // open: Qn, preset
  Multiplexer multiplexer_6 (.in0(multiplexer_5_out), .in1(DATA[5]), .out(multiplexer_6_out));  // open: sel
  Multiplexer multiplexer_7 (.in0(DATA_OUT[4]), .in1(DATA_OUT[5]), .out(multiplexer_7_out), .sel(SHIFT_ENABLE));
  D_Flip_Flop d_ff_4 (.D(multiplexer_8_out), .clk(CLK), .Q(DATA_OUT[4]), .reset(reset));  // open: Qn, preset
  Multiplexer multiplexer_8 (.in0(multiplexer_7_out), .in1(DATA[4]), .out(multiplexer_8_out));  // open: sel
  Multiplexer multiplexer_9 (.in0(DATA_OUT[3]), .in1(DATA_OUT[4]), .out(multiplexer_9_out), .sel(SHIFT_ENABLE));
  D_Flip_Flop d_ff_5 (.D(multiplexer_10_out), .clk(CLK), .Q(DATA_OUT[3]), .reset(reset));  // open: Qn, preset
  Multiplexer multiplexer_10 (.in0(multiplexer_9_out), .in1(DATA[3]), .out(multiplexer_10_out));  // open: sel
  Multiplexer multiplexer_11 (.in0(DATA_OUT[2]), .in1(DATA_OUT[3]), .out(multiplexer_11_out), .sel(SHIFT_ENABLE));
  D_Flip_Flop d_ff_6 (.D(multiplexer_12_out), .clk(CLK), .Q(DATA_OUT[2]), .reset(reset));  // open: Qn, preset
  Multiplexer multiplexer_12 (.in0(multiplexer_11_out), .in1(DATA[2]), .out(multiplexer_12_out));  // open: sel
  Multiplexer multiplexer_13 (.in0(DATA_OUT[1]), .in1(DATA_OUT[2]), .out(multiplexer_13_out), .sel(SHIFT_ENABLE));
  D_Flip_Flop d_ff_7 (.D(multiplexer_14_out), .clk(CLK), .Q(DATA_OUT[1]), .reset(reset));  // open: Qn, preset
  Multiplexer multiplexer_14 (.in0(multiplexer_13_out), .in1(DATA[1]), .out(multiplexer_14_out));  // open: sel
  Multiplexer multiplexer_15 (.in0(DATA_OUT[0]), .in1(DATA_OUT[1]), .out(multiplexer_15_out), .sel(SHIFT_ENABLE));
  D_Flip_Flop d_ff_8 (.D(multiplexer_16_out), .clk(CLK), .Q(DATA_OUT[0]), .reset(reset));  // open: Qn, preset
  Multiplexer multiplexer_16 (.in0(multiplexer_15_out), .in1(DATA[0]), .out(multiplexer_16_out));  // open: sel
endmodule
